// Logisim project MEM.circ as structural Verilog
// 1x1
module RAM_1x1a (
  input  R_W,
  input  adress,
  input  CLK,
  input  \input ,
  input  CLR,
  output \output 
);

  wire and_1_out, FF_D_q;

  D_Flip_Flop #(.Pre_Clr_Positions("LEGACY"), .NewFFLayout("false")) FF_D (
    .clk(and_1_out), .D(\input ), .Q(FF_D_q), .reset(CLR));  // open: Qn, preset
  and and_1 (and_1_out, adress, R_W, CLK);
  and and_2 (\output , adress, FF_D_q);
endmodule

// 1x1
module RAM_1x1b (
  input  R_W,
  input  adress,
  input  CLK,
  input  \input ,
  input  CLR,
  output \output 
);

  wire and_1_out, FF_D_q;

  D_Flip_Flop #(.Pre_Clr_Positions("LEGACY"), .NewFFLayout("false")) FF_D (
    .clk(and_1_out), .D(\input ), .Q(FF_D_q), .reset(CLR));  // open: Qn, preset
  and and_1 (and_1_out, adress, R_W, CLK);
  and and_2 (\output , adress, FF_D_q);
endmodule

// 1x1
module RAM_1x1c (
  input  R_W,
  input  adress,
  input  CLK,
  input  CLR,
  input  \input ,
  output \output 
);

  RAM_1x1b ram_1x1b_1 (.R_W(R_W), .CLK(CLK), .CLR(CLR), .adress(adress), .\output (\output ), .\input (\input ));
endmodule

module RAM_1x2a (
  input  adress,
  input  R_W,
  input  CLK,
  input  CLR,
  input  input_0,
  input  input_1,
  output output_0,
  output output_1
);

  RAM_1x1a ram_1x1a_1 (.R_W(R_W), .CLK(CLK), .CLR(CLR), .adress(adress), .\output (output_1), .\input (input_1));
  RAM_1x1a ram_1x1a_2 (.R_W(R_W), .CLK(CLK), .CLR(CLR), .adress(adress), .\output (output_0), .\input (input_0));
endmodule

// 1x2
module RAM_1x2b (
  input  adress,
  input  R_W,
  input  CLK,
  input  CLR,
  input  [1:0] \input ,
  output [1:0] \output 
);

  RAM_1x1a ram_1x1a_1 (.R_W(R_W), .CLK(CLK), .CLR(CLR), .adress(adress), .\output (\output [1]), .\input (\input [1]));
  RAM_1x1a ram_1x1a_2 (.R_W(R_W), .CLK(CLK), .CLR(CLR), .adress(adress), .\output (\output [0]), .\input (\input [0]));
endmodule

module RAM_1x2c (
  input  R_W,
  input  adress,
  input  CLK,
  input  CLR,
  input  [1:0] \input ,
  output [1:0] \output 
);

  RAM_1x2b ram_1x2b_1 (.R_W(R_W), .CLK(CLK), .CLR(CLR), .adress(adress), .\output (\output ), .\input (\input ));
endmodule

// 1x4
module RAM_1x4a (
  input  adress,
  input  R_W,
  input  CLK,
  input  CLR,
  input  [3:0] \input ,
  output [3:0] \output 
);

  RAM_1x1c ram_1x1c_1 (.R_W(R_W), .CLK(CLK), .CLR(CLR), .adress(adress), .\output (\output [3]), .\input (\input [3]));
  RAM_1x1c ram_1x1c_2 (.R_W(R_W), .CLK(CLK), .CLR(CLR), .adress(adress), .\output (\output [2]), .\input (\input [2]));
  RAM_1x1c ram_1x1c_3 (.R_W(R_W), .CLK(CLK), .CLR(CLR), .adress(adress), .\output (\output [1]), .\input (\input [1]));
  RAM_1x1c ram_1x1c_4 (.R_W(R_W), .CLK(CLK), .CLR(CLR), .adress(adress), .\output (\output [0]), .\input (\input [0]));
endmodule

// 1x4
module RAM_1x4b (
  input  R_W,
  input  adress,
  input  CLK,
  input  CLR,
  input  [3:0] \input ,
  output [3:0] \output 
);

  RAM_1x4a ram_1x4a_1 (.R_W(R_W), .CLK(CLK), .CLR(CLR), .adress(adress), .\output (\output ), .\input (\input ));
endmodule

// 2x1
module RAM_2x1a (
  input  R_W,
  input  adress,
  input  CLK,
  input  CLR,
  input  \input ,
  output \output 
);

  wire demultiplexer_1_out0, demultiplexer_1_out1, ram_1x1b_1_output, ram_1x1b_2_output;

  RAM_1x1b ram_1x1b_1 (
    .R_W(R_W), .CLK(CLK), .CLR(CLR), .adress(demultiplexer_1_out0), .\output (ram_1x1b_1_output),
    .\input (\input ));
  RAM_1x1b ram_1x1b_2 (
    .R_W(R_W), .CLK(CLK), .CLR(CLR), .adress(demultiplexer_1_out1), .\output (ram_1x1b_2_output),
    .\input (\input ));
  Demultiplexer #(.enable("false")) demultiplexer_1 (
    .out0(demultiplexer_1_out0), .out1(demultiplexer_1_out1), .in(1'b1), .sel(adress));
  Multiplexer #(.enable("false")) multiplexer_1 (
    .in0(ram_1x1b_1_output), .in1(ram_1x1b_2_output), .out(\output ), .sel(adress));
endmodule

// 2x2
module RAM_2x2a (
  input  adress,
  input  R_W,
  input  CLK,
  input  CLR,
  input  [1:0] \input ,
  output [1:0] \output 
);

  RAM_2x1a ram_2x1a_1 (.R_W(R_W), .CLK(CLK), .CLR(CLR), .adress(adress), .\input (\input [1]), .\output (\output [1]));
  RAM_2x1a ram_2x1a_2 (.R_W(R_W), .CLK(CLK), .CLR(CLR), .adress(adress), .\input (\input [0]), .\output (\output [0]));
endmodule

// 4x4
module RAM_4x4a (
  input  [1:0] adress,
  input  R_W,
  input  [3:0] \input ,
  input  CLK,
  input  CLR,
  output [3:0] \output 
);

  wire demultiplexer_1_out0, demultiplexer_1_out1, demultiplexer_1_out2, demultiplexer_1_out3;
  wire [3:0] ram_1x4a_1_output, ram_1x4a_2_output, ram_1x4a_3_output, ram_1x4a_4_output;

  Demultiplexer #(.select(2), .enable("false")) demultiplexer_1 (
    .out0(demultiplexer_1_out0), .out1(demultiplexer_1_out1), .out2(demultiplexer_1_out2),
    .out3(demultiplexer_1_out3), .in(1'b1), .sel(adress));
  RAM_1x4a ram_1x4a_1 (
    .R_W(R_W), .CLK(CLK), .CLR(CLR), .adress(demultiplexer_1_out0), .\output (ram_1x4a_1_output),
    .\input (\input ));
  RAM_1x4a ram_1x4a_2 (
    .R_W(R_W), .CLK(CLK), .CLR(CLR), .adress(demultiplexer_1_out1), .\output (ram_1x4a_2_output),
    .\input (\input ));
  RAM_1x4a ram_1x4a_3 (
    .R_W(R_W), .CLK(CLK), .CLR(CLR), .adress(demultiplexer_1_out2), .\output (ram_1x4a_3_output),
    .\input (\input ));
  RAM_1x4a ram_1x4a_4 (
    .R_W(R_W), .CLK(CLK), .CLR(CLR), .adress(demultiplexer_1_out3), .\output (ram_1x4a_4_output),
    .\input (\input ));
  Multiplexer #(.select(2), .width(4), .enable("false")) multiplexer_1 (
    .in0(ram_1x4a_1_output), .in1(ram_1x4a_2_output), .in2(ram_1x4a_3_output), .in3(ram_1x4a_4_output),
    .out(\output ), .sel(adress));
endmodule

// 4x8
module RAM_4x8a (
  input  R_W,
  input  [1:0] adress,
  input  CLK,
  input  CLR,
  input  [7:0] \input ,
  output [7:0] \output 
);

  RAM_4x4a ram_4x4a_1 (
    .R_W(R_W), .CLK(CLK), .CLR(CLR), .adress(adress), .\input (\input [7:4]), .\output (\output [7:4]));
  RAM_4x4a ram_4x4a_2 (
    .R_W(R_W), .CLK(CLK), .CLR(CLR), .adress(adress), .\input (\input [3:0]), .\output (\output [3:0]));
endmodule

// 4x8
module RAM_4x8b (
  input  R_W,
  input  [1:0] adress,
  input  CLK,
  input  [7:0] \input ,
  input  CLR,
  output [7:0] \output 
);

  RAM_4x8a ram_4x8a_1 (.R_W(R_W), .CLK(CLK), .CLR(CLR), .adress(adress), .\input (\input ), .\output (\output ));
endmodule

// 1x8
module RAM_1x8a (
  input  adress,
  input  R_W,
  input  CLK,
  input  CLR,
  input  [7:0] \input ,
  output [7:0] \output 
);

  RAM_1x1c ram_1x1c_1 (.R_W(R_W), .CLK(CLK), .CLR(CLR), .adress(adress), .\output (\output [3]), .\input (\input [3]));
  RAM_1x1c ram_1x1c_2 (.R_W(R_W), .CLK(CLK), .CLR(CLR), .adress(adress), .\output (\output [4]), .\input (\input [4]));
  RAM_1x1c ram_1x1c_3 (.R_W(R_W), .CLK(CLK), .CLR(CLR), .adress(adress), .\output (\output [2]), .\input (\input [2]));
  RAM_1x1c ram_1x1c_4 (.R_W(R_W), .CLK(CLK), .CLR(CLR), .adress(adress), .\output (\output [5]), .\input (\input [5]));
  RAM_1x1c ram_1x1c_5 (.R_W(R_W), .CLK(CLK), .CLR(CLR), .adress(adress), .\output (\output [1]), .\input (\input [1]));
  RAM_1x1c ram_1x1c_6 (.R_W(R_W), .CLK(CLK), .CLR(CLR), .adress(adress), .\output (\output [6]), .\input (\input [6]));
  RAM_1x1c ram_1x1c_7 (.R_W(R_W), .CLK(CLK), .CLR(CLR), .adress(adress), .\output (\output [0]), .\input (\input [0]));
  RAM_1x1c ram_1x1c_8 (.R_W(R_W), .CLK(CLK), .CLR(CLR), .adress(adress), .\output (\output [7]), .\input (\input [7]));
endmodule

module RAM_1x8b (
  input  R_W,
  input  adress,
  input  CLK,
  input  CLR,
  input  [7:0] \input ,
  output [7:0] \output 
);

  RAM_1x8a ram_1x8a_1 (.R_W(R_W), .CLK(CLK), .CLR(CLR), .adress(adress), .\output (\output ), .\input (\input ));
endmodule

// 8x8
module RAM_8x8a (
  input  [2:0] adress,
  input  R_W,
  input  [7:0] \input ,
  input  CLK,
  input  CLR,
  output [7:0] \output 
);

  wire demultiplexer_1_out0, demultiplexer_1_out1, demultiplexer_1_out2, demultiplexer_1_out3,
       demultiplexer_1_out4, demultiplexer_1_out5, demultiplexer_1_out6, demultiplexer_1_out7;
  wire [7:0] ram_1x8a_1_output, ram_1x8a_2_output, ram_1x8a_3_output, ram_1x8a_4_output, ram_1x8a_5_output,
       ram_1x8a_6_output, ram_1x8a_7_output, ram_1x8a_8_output;

  Demultiplexer #(.select(3), .enable("false")) demultiplexer_1 (
    .out0(demultiplexer_1_out0), .out1(demultiplexer_1_out1), .out2(demultiplexer_1_out2),
    .out3(demultiplexer_1_out3), .out4(demultiplexer_1_out4), .out5(demultiplexer_1_out5),
    .out6(demultiplexer_1_out6), .out7(demultiplexer_1_out7), .in(1'b1), .sel(adress));
  RAM_1x8a ram_1x8a_1 (
    .R_W(R_W), .CLK(CLK), .CLR(CLR), .adress(demultiplexer_1_out0), .\output (ram_1x8a_1_output),
    .\input (\input ));
  RAM_1x8a ram_1x8a_2 (
    .R_W(R_W), .CLK(CLK), .CLR(CLR), .adress(demultiplexer_1_out1), .\output (ram_1x8a_2_output),
    .\input (\input ));
  RAM_1x8a ram_1x8a_3 (
    .R_W(R_W), .CLK(CLK), .CLR(CLR), .adress(demultiplexer_1_out2), .\output (ram_1x8a_3_output),
    .\input (\input ));
  RAM_1x8a ram_1x8a_4 (
    .R_W(R_W), .CLK(CLK), .CLR(CLR), .adress(demultiplexer_1_out3), .\output (ram_1x8a_4_output),
    .\input (\input ));
  RAM_1x8a ram_1x8a_5 (
    .R_W(R_W), .CLK(CLK), .CLR(CLR), .adress(demultiplexer_1_out4), .\output (ram_1x8a_5_output),
    .\input (\input ));
  RAM_1x8a ram_1x8a_6 (
    .R_W(R_W), .CLK(CLK), .CLR(CLR), .adress(demultiplexer_1_out5), .\output (ram_1x8a_6_output),
    .\input (\input ));
  RAM_1x8a ram_1x8a_7 (
    .R_W(R_W), .CLK(CLK), .CLR(CLR), .adress(demultiplexer_1_out6), .\output (ram_1x8a_7_output),
    .\input (\input ));
  RAM_1x8a ram_1x8a_8 (
    .R_W(R_W), .CLK(CLK), .CLR(CLR), .adress(demultiplexer_1_out7), .\output (ram_1x8a_8_output),
    .\input (\input ));
  Multiplexer #(.select(3), .width(8), .enable("false")) multiplexer_1 (
    .in0(ram_1x8a_1_output), .in1(ram_1x8a_2_output), .in2(ram_1x8a_3_output), .in3(ram_1x8a_4_output),
    .in4(ram_1x8a_5_output), .in5(ram_1x8a_6_output), .in6(ram_1x8a_7_output), .in7(ram_1x8a_8_output),
    .out(\output ), .sel(adress));
endmodule

module RAM_8x8b (
  input  R_W,
  input  [2:0] adress,
  input  CLK,
  input  [7:0] \input ,
  input  CLR,
  output [7:0] \output 
);

  RAM_8x8a ram_8x8a_1 (.R_W(R_W), .CLK(CLK), .CLR(CLR), .adress(adress), .\input (\input ), .\output (\output ));
endmodule
